# Fritzing sketch Doug - tapeDuino Integrated v3 stripped (saved by Fritzing 0.9.3b)
breadboards: 2

parts:
  C1 = Ceramic Capacitor [capacitance=0.1µF package="100 mil [THT, multilayer]"]
  R2 = Resistor [tolerance=±5% resistance=10k package=THT]
  MT8870-DE = IC, DIP package, 18 pins [chip_label=8870 spacing=300mil]
  XTAL1 = Crystal [frequency=4MHz package=THT]
  C2 = Ceramic Capacitor [capacitance=0.1µF package="100 mil [THT, multilayer]"]
  R4 = Resistor [tolerance=±5% resistance=5.1k package=THT]
  R6 = Trimmer Potentiometer [maximum_resistance=100kΩ package=THT]
  R7 = Trimmer Potentiometer [maximum_resistance=100kΩ package=THT]
  R8 = Resistor [tolerance=±5% resistance=330 package=THT]
  R9 = Resistor [tolerance=±5% resistance=330 package=THT]
  R10 = Resistor [tolerance=±5% resistance=330 package=THT]
  R11 = Resistor [tolerance=±5% resistance=330 package=THT]
  LED1 = LED - 5mm [color="Red (633nm)" package="5 mm [THT]"]
  LED2 = LED - 5mm [color="Red (633nm)" package="5 mm [THT]"]
  LED3 = LED - 5mm [color="Red (633nm)" package="5 mm [THT]"]
  LED4 = LED - 5mm [color="Red (633nm)" package="5 mm [THT]"]
  LED5 = LED - 5mm [color="Yellow (574nm)" package="5 mm [THT]"]
  R12 = Resistor [tolerance=±5% resistance=330 package=THT]
  R14 = Resistor [tolerance=±5% resistance=330 package=THT]
  R15 = Resistor [tolerance=±5% resistance=330 package=THT]
  R16 = Trimmer Potentiometer [maximum_resistance=20kΩ package=THT]
  R17 = Resistor [tolerance=±5% resistance=300k package=THT]
  J1 = male pin header, 3 pins [form="♂ (male)"]
  3_5MM_PHONE = Audio Jack (TRS) 3.5mm [package="4Ucon 08780 [THT]"]
  3_5MM_PHONE1 = Audio Jack (TRS) 3.5mm [package="4Ucon 08780 [THT]"]
  5V = DC Power [voltage=5]  # not connected
  Arduino1 = Arduino Uno (Rev3)
  5V1 = DC Power [voltage=5]  # not connected
  5V_2 = DC Power [voltage=5]  # not connected

nets (from the breadboard view):
  N1: C1.0, 3_5MM_PHONE.Ring
  N2: C1.1, R6.leg1, R6.leg2
  N3: R2.Pin_0, R6.wiper
  N4: R2.Pin_1, MT8870-DE.pin2, R7.leg1
  N5: MT8870-DE.pin1, MT8870-DE.pin4
  N6: MT8870-DE.pin3, R7.wiper
  N7: MT8870-DE.pin7, XTAL1.pin_0
  N8: MT8870-DE.pin8, XTAL1.pin_1
  N9: MT8870-DE.pin9, 3_5MM_PHONE.Sleeve, Arduino1.GND
  N10: MT8870-DE.pin10, MT8870-DE.pin18, C2.0, R12.Pin_1, 3_5MM_PHONE1.Sleeve
  N11: MT8870-DE.pin11, LED4.anode
  N12: MT8870-DE.pin12, LED3.anode, Arduino1.D4
  N13: MT8870-DE.pin13, LED2.anode
  N14: MT8870-DE.pin14, LED1.anode
  N15: MT8870-DE.pin15, Arduino1.D2
  N16: MT8870-DE.pin16, R4.Pin_1
  N17: MT8870-DE.pin17, C2.1, R4.Pin_0
  N18: R8.Pin_0, R9.Pin_0, R10.Pin_0, R11.Pin_0, LED5.anode
  N19: R8.Pin_1, LED1.cathode
  N20: R9.Pin_1, LED2.cathode
  N21: R10.Pin_1, LED3.cathode
  N22: R11.Pin_1, LED4.cathode
  N23: LED5.cathode, R12.Pin_0
  N24: R14.Pin_0, R15.Pin_0, J1.pin2
  N25: R16.leg1, J1.pin1
  N26: R16.wiper, R17.Pin_0, 3_5MM_PHONE1.Ring
  N27: R17.Pin_1, J1.pin3
