# Fritzing sketch Identificador de Chamada 0.1.1 (saved by Fritzing 0.9.3b)
circuit board: 3.5cm x 4cm
breadboards: 1

parts:
  D13 = Zener Diode [part_number=1N4732A breakdown_voltage=20V package="300 mil [THT]"]
  D14 = Zener Diode [part_number=1N4732A breakdown_voltage=20V package="300 mil [THT]"]
  R25 = Resistor [tolerance=±5% resistance=20k package=THT]
  R26 = Resistor [tolerance=±5% resistance=20k package=THT]
  R27 = Resistor [tolerance=±5% resistance=20k package=THT]
  U6 = Optocoupler [package=THT]
  C8 = Ceramic Capacitor [capacitance=10nF voltage=0.1kV package="200 mil [THT, multilayer]"]
  R28 = Resistor [tolerance=±5% resistance=50k package=THT]
  D15 = Rectifier Diode [part_number=1N4148 package="300 mil [THT]"]
  J16 = male pin header, 8 pins [form="♂ (male)"]
  J17 = male pin header, 8 pins [form="♂ (male)"]

nets:
  N1: D13.cathode, U6.Pin_1, D15.cathode
  N2: D13.anode, D14.cathode
  N3: D14.anode, R28.Pin_1
  GND: R25.Pin_0, U6.Pin_4, J17.pin8
  N4: R25.Pin_1, R26.Pin_0, U6.Pin_6
  5V: R26.Pin_1, R27.Pin_1, J17.pin1
  Tel-Ring: R27.Pin_0, U6.Pin_5, J17.pin4
  Tel-Minus: U6.Pin_2, D15.anode, J16.pin3
  N5: C8.0, R28.Pin_0
  Tel-Plus: C8.1, J16.pin6
  phone-out-ring: J16.pin1
  phone-ring: J16.pin2
  Tel-Audio-Plus: J16.pin4
  Tel-Audio-Minus: J16.pin5
  phone-tip: J16.pin7
  phone-out-tip: J16.pin8

notes:
  V 0.1.1
  Identificador
  de Chamada
