# Fritzing sketch Retificador Audio V 0.1.2 (saved by Fritzing 0.9.3b)
circuit board: 5.98645cm x 4.04029cm
breadboards: 1

parts:
  J11 = female pin header, 2 pins [form="♀ (female)"]
  J12 = female pin header, 2 pins [form="♀ (female)"]
  J13 = female pin header, 2 pins [form="♀ (female)"]
  J14 = female pin header, 2 pins [form="♀ (female)"]
  D10 = Rectifier Diode [part_number=1N4001 package="300 mil [THT]"]
  D11 = Rectifier Diode [part_number=1N4001 package="300 mil [THT]"]
  D12 = Rectifier Diode [part_number=1N4001 package="300 mil [THT]"]
  D13 = Rectifier Diode [part_number=1N4001 package="300 mil [THT]"]
  U2 = V18ZA2P [package=v18za2p]
  F3 = FUSE [package=fuse_5mm]
  F4 = FUSE [package=fuse_5mm]
  C4 = Ceramic Capacitor [capacitance=10nF voltage=0.1kV package="200 mil [THT, multilayer]"]
  C5 = Ceramic Capacitor [capacitance=10nF voltage=0.1kV package="200 mil [THT, multilayer]"]
  R21 = Resistor [tolerance=±5% resistance=50k package=THT]
  R22 = Resistor [tolerance=±5% resistance=50k package=THT]
  R23 = Resistor [tolerance=±5% resistance=50k package=THT]
  R24 = Resistor [tolerance=±5% resistance=50k package=THT]
  D14 = Rectifier Diode [part_number=1N4148 package="300 mil [THT]"]
  D15 = Rectifier Diode [part_number=1N4148 package="300 mil [THT]"]
  J15 = male pin header, 10 pins [form="♂ (male)"]

nets:
  phone-ring: J11.pin1, D10.anode, D13.cathode, U2.P$1, F4.1, J15.pin3
  phone-tip: J12.pin2, D11.cathode, D12.anode, U2.P$2, F3.1, J15.pin8
  phone-out-ring: J13.pin1, F4.2, J15.pin2
  phone-out-tip: J14.pin2, F3.2, J15.pin9
  Tel-Plus: D10.cathode, D12.cathode, C5.1, J15.pin7
  Tel-Minus: D11.anode, D13.anode, C4.1, J15.pin4
  N1: C4.0, R22.Pin_0
  N2: C5.0, R24.Pin_0
  N3: R21.Pin_0, R22.Pin_1, D15.anode
  Tel-Audio-Minus: R21.Pin_1, J15.pin6
  N4: R23.Pin_0, R24.Pin_1, D14.anode
  Tel-Audio-Plus: R23.Pin_1, J15.pin5
  N5: D14.cathode, D15.cathode

notes:
  V 0.1.2
  Smart Bina
  Retificador
  V 0.1.3
