# Fritzing sketch Retificador V 0.1.1 (saved by Fritzing 0.9.3b)
circuit board: 4.46062cm x 3.99731cm
breadboards: 1

parts:
  J11 = female pin header, 2 pins [form="♀ (female)"]
  J12 = female pin header, 2 pins [form="♀ (female)"]
  J13 = female pin header, 2 pins [form="♀ (female)"]
  J14 = female pin header, 2 pins [form="♀ (female)"]
  D10 = Rectifier Diode [part_number=1N4001 package="300 mil [THT]"]
  D11 = Rectifier Diode [part_number=1N4001 package="300 mil [THT]"]
  D12 = Rectifier Diode [part_number=1N4001 package="300 mil [THT]"]
  D13 = Rectifier Diode [part_number=1N4001 package="300 mil [THT]"]
  U2 = V18ZA2P [package=v18za2p]
  F3 = FUSE [package=fuse_5mm]
  F4 = FUSE [package=fuse_5mm]
  J15 = male pin header, 8 pins [form="♂ (male)"]

nets:
  phone-ring: J11.pin1, D10.anode, D13.cathode, U2.P$1, F4.1, J15.pin2
  phone-tip: J12.pin2, D11.cathode, D12.anode, U2.P$2, F3.1, J15.pin7
  phone-out-ring: J13.pin1, F4.2, J15.pin1
  phone-out-tip: J14.pin2, F3.2, J15.pin8
  Tel-Plus: D10.cathode, D12.cathode, J15.pin6
  Tel-Minus: D11.anode, D13.anode, J15.pin3
  Tel-Audio-Plus: J15.pin4
  Tel-Audio-Minus: J15.pin5

notes:
  V 0.1.1
  Retificador
  Smart Bina
