# Fritzing sketch Smart Bina Shield (saved by Fritzing 0.9.3b)
circuit board: 6.88566cm x 5.36311cm

parts:
  J16 = male pin header, 8 pins [form="♂ (male)"]
  MT8870-DE2 = IC, DIP package, 18 pins [chip_label=8870]
  C6 = Ceramic Capacitor [capacitance=10nF voltage=0.1kV package="200 mil [THT, multilayer]"]
  C7 = Ceramic Capacitor [capacitance=10nF voltage=0.1kV package="200 mil [THT, multilayer]"]
  R33 = Resistor [tolerance=±5% resistance=10k package=THT]
  R34 = Resistor [tolerance=±5% resistance=10k package=THT]
  R35 = Resistor [tolerance=±5% resistance=10k package=THT]
  R36 = Resistor [tolerance=±5% resistance=390k package=THT]
  XTAL2 = Crystal [frequency="16 Mhz" package=THT]
  Componente1 = Arduino Prototyping Shield

nets:
  phone-ring: J16.pin1, Componente1.N$44
  phone-out-ring: J16.pin2, Componente1.N$56
  Tel-Minus: J16.pin3, Componente1.N$68
  Tel-Audio-Plus: J16.pin4, MT8870-DE2.pin1, R34.Pin_0, R35.Pin_0, Componente1.N$78, Componente1.N$79, Componente1.N$80, Componente1.N$84, Componente1.N$304, Componente1.N$422, Componente1.N$431
  Tel-Audio-Minus: J16.pin5, MT8870-DE2.pin2, R33.Pin_0, Componente1.N$16, Componente1.N$29, Componente1.N$67, Componente1.N$74, Componente1.N$165
  Tel-Plus: J16.pin6, Componente1.N$92
  phone-out-tip: J16.pin7, Componente1.N$35
  phone-tip: J16.pin8, Componente1.N$30
  N1: MT8870-DE2.pin3, R35.Pin_1, Componente1.N$305, Componente1.N$434
  N2: MT8870-DE2.pin4, R33.Pin_1, R34.Pin_1, Componente1.N$241, Componente1.N$269, Componente1.N$417
  N3: MT8870-DE2.pin5, Componente1.N$267
  N4: MT8870-DE2.pin6, Componente1.N$268
  N5: MT8870-DE2.pin7, XTAL2.pin_1, Componente1.N$238, Componente1.N$239
  N6: MT8870-DE2.pin8, XTAL2.pin_0, Componente1.N$230, Componente1.N$234, Componente1.N$236
  GND: MT8870-DE2.pin9, C6.1, Componente1.GND, Componente1.N$235, Componente1.N$285
  MT8870 TOE: MT8870-DE2.pin10, Componente1.D13, Componente1.N$259
  MT8870 Q1: MT8870-DE2.pin11, Componente1.A0, Componente1.N$261
  MT8870 Q2: MT8870-DE2.pin12, Componente1.A1, Componente1.N$262
  MT8870 Q3: MT8870-DE2.pin13, Componente1.A2, Componente1.N$263
  MT8870 Q4: MT8870-DE2.pin14, Componente1.A3, Componente1.N$298
  MT8870 StD: MT8870-DE2.pin15, Componente1.D2, Componente1.N$297
  N7: MT8870-DE2.pin16, R36.Pin_0, Componente1.N$299, Componente1.N$361
  N8: MT8870-DE2.pin17, C7.1, R36.Pin_1, Componente1.N$318, Componente1.N$319, Componente1.N$356
  5V: MT8870-DE2.pin18, C6.0, C7.0, Componente1.+5V, Componente1.N$17, Componente1.N$291, Componente1.N$381
  Hook-ctrl: Componente1.A4
  LED-Tocando: Componente1.D8
  LED-Ocupado: Componente1.D9
  LED-Monitor: Componente1.D10
  Tel-Ring: Componente1.D3
  tel-01: Componente1.D4
  tel-02: Componente1.D5
  KeyBoard-Mode: Componente1.D6
  LED-Livre: Componente1.A5
